# Fritzing sketch SchemaFritzing (saved by Fritzing 0.9.3b)
breadboards: 1

parts:
  U2 = HC-SR04 [chip_label=IC package="SIP (Single Inline) [THT]"]
  LED1 = LED - 5mm [color="Green (555nm)" package="5 mm [THT]"]
  R1 = Resistor [tolerance=±5% resistance=220 package=THT]
  LED2 = LED - 5mm [color="Green (555nm)" package="5 mm [THT]"]
  R2 = Resistor [tolerance=±5% resistance=220 package=THT]
  LED3 = LED - 5mm [color="Red (633nm)" package="5 mm [THT]"]
  R3 = Resistor [tolerance=±5% resistance=220 package=THT]
  S1 = Pushbutton [package="[THT]"]
  R4 = Resistor [tolerance=±5% resistance=10k package=THT]
  S2 = Pushbutton [package="[THT]"]
  R5 = Resistor [tolerance=±5% resistance=10k package=THT]
  PIR2 = PIR sensor
  Componente1 = Arduino Uno (Rev3)

nets:
  VCC: U2.Vcc, S1.Pin_1, S1.Pin_2, S2.Pin_1, S2.Pin_2, PIR2.VDD, Componente1.5V
  N1: U2.Trig, Componente1.D4
  N2: U2.Echo, Componente1.D7
  GND: U2.GND, LED1.cathode, LED2.cathode, LED3.cathode, R4.Pin_1, R5.Pin_1, PIR2.GND, Componente1.GND
  N3: LED1.anode, R1.Pin_0
  N4: R1.Pin_1, Componente1.D9_PWM
  N5: LED2.anode, R2.Pin_0
  N6: R2.Pin_1, Componente1.D10_PWM/SS
  N7: LED3.anode, R3.Pin_0
  N8: R3.Pin_1, Componente1.D11_PWM/MOSI
  N9: S1.Pin_3, S1.Pin_4, R4.Pin_0, Componente1.D0/RX
  N10: S2.Pin_3, S2.Pin_4, R5.Pin_0, Componente1.D1/TX
  N11: PIR2.SIG, Componente1.D2

custom parts:
  HC-SR04: HC-SR04 ultrasound distance sensor
